# Fritzing sketch MIDIDouserController (saved by Fritzing 0.9.2b)
circuit board: 5cm x 10cm
breadboards: 1

parts:
  Power_plug1 = Power plug
  L293D = L293D [package=THT]
  L293D_2 = L293D [package=THT]
  Arduino_Nano = Arduino Nano (Rev3.0)
  J1 = Screw terminal - 2 pins [package=THT]
  J2 = Screw terminal - 2 pins [package=THT]
  J3 = Screw terminal - 2 pins [package=THT]
  SW1 = DIP SWITCH [package=dipswitch-02]

nets:
  GND: Power_plug1.GND, L293D.0V, L293D_2.0V, Arduino_Nano.GND, SW1.3, SW1.4
  N1: Power_plug1.VCC, L293D.+Vmotor, L293D_2.+Vmotor
  N2: L293D.Enable_1, Arduino_Nano.D3
  N3: L293D.In_1, Arduino_Nano.D4
  N4: L293D.Out_1_(_Controlled_by_Enable_1_), J1.pin2
  N5: L293D.Out_2_(_Controlled_by_Enable_1_), J1.pin1
  N6: L293D.In_2, Arduino_Nano.D2
  N7: L293D.Enable_2, Arduino_Nano.D9
  N8: L293D.In_3, Arduino_Nano.D7
  N9: L293D.Out_3_(_Controlled_by_Enable_2_), J2.pin2
  N10: L293D.Out_4_(_Controlled_by_Enable_2_), J2.pin1
  N11: L293D.In_4, Arduino_Nano.D8
  N12: L293D.+V, L293D_2.+V, Arduino_Nano.5V
  N13: L293D_2.Enable_2, Arduino_Nano.D10
  N14: L293D_2.In_3, Arduino_Nano.D5
  N15: L293D_2.Out_3_(_Controlled_by_Enable_2_), J3.pin2
  N16: L293D_2.Out_4_(_Controlled_by_Enable_2_), J3.pin1
  N17: L293D_2.In_4, Arduino_Nano.D12/MISO
  N18: Arduino_Nano.D6, SW1.2
  N19: Arduino_Nano.D11/MOSI, SW1.1

notes:
  Version 1.0
  Douser Controller
